# Fritzing sketch DHT11 (saved by Fritzing 1.0.2b)
breadboards: 1

parts:
  Raspberry_Pi_1 = Raspberry Pi 4 [part_number=RPI-4-b]
  DHT1 = Humidity and Temperature Sensor DHT11
  R1 = Resistor [tolerance=±5% power=0.25W resistance=220 package=THT]

nets:
  3V3: Raspberry_Pi_1.3v3, DHT1.Vcc, R1.Pin_0
  N1: Raspberry_Pi_1.GPIO14, DHT1.Data-signal, R1.Pin_1
  N2: Raspberry_Pi_1.GND, DHT1.GND_2

custom parts:
  Raspberry Pi 4: The RPi4, a faster version of the awesome Raspberry Pi 2 B ARM Board with 40 pin gpio. Ready for special Raspberry Pi B+ and RPi2 Hat (Hardware attached (on) top)
  Humidity and Temperature Sensor DHT11: Digital relative humidity & temperature sensor DHT11
