# Fritzing sketch arduino_fan_control (saved by Fritzing 1.0.2b)
circuit board: 8.46667cm x 5.64444cm
breadboards: 1

parts:
  Parça1 = Arduino Uno (Rev3)
  R1 = Resistor [tolerance=±5% power=0.25W resistance=440 package=THT]
  LED1 = RGB LED (com. cathode, rgb) [color="Red (633nm)" current=0.030A package="5 mm [THT]"]
  R2 = Resistor [tolerance=±5% power=0.25W resistance=220 package=THT]
  F1 = Fan - Ventilador [package=THT]
  R3 = Resistor [tolerance=±5% power=0.25W resistance=1k package=THT]
  BC337_NPN = NPN-Transistor [package="TO92 [THT]"]
  Q4 = PNP-Transistor [package="TO92 [THT]"]
  R4 = Resistor [tolerance=±5% resistance=220 package="0402 [SMD]"]
  R5 = Resistor [tolerance=±5% resistance=220 package="0402 [SMD]"]
  Raspberry_Pi_1 = Raspberry Pi 4 [part_number=RPI-4-b]  # not connected

nets:
  N1: Parça1.D9_PWM, R1.Pin_1, R2.Pin_0, R3.Pin_1
  5V: Parça1.5V, F1.5V, Q4.E
  N2: Parça1.GND, BC337_NPN.E
  N3: R1.Pin_0, BC337_NPN.B
  N4: LED1.red_anode, R2.Pin_1
  N5: LED1.common_cathode, R5.Pin_1
  N6: LED1.green_anode, R4.Pin_0
  N7: F1.GND, BC337_NPN.C, R5.Pin_0
  N8: R3.Pin_0, Q4.B
  N9: Q4.C, R4.Pin_1

custom parts:
  Fan - Ventilador: Ventilador de 2 pines, se encuentra comunmente en computadoras de escritorio
  NPN-Transistor: A standard NPN-transistor
  PNP-Transistor: A standard PNP signal transistor
  Raspberry Pi 4: The RPi4, a faster version of the awesome Raspberry Pi 2 B ARM Board with 40 pin gpio. Ready for special Raspberry Pi B+ and RPi2 Hat (Hardware attached (on) top)

// code stored in the sketch: arduino_fan_control.ino
int lastValue = 0; 


void setup() {
  pinMode(9, OUTPUT); // PWM 
  // Pin 9 ve 10  PWM 31.25 kHz olarak ayarla
  TCCR1B = TCCR1B & 0b11111000 | 0x01;
  Serial.begin(9600);
  Serial.println("Fan kontrolu basladi");
}


void loop() {
  if (Serial.available() > 1) {
    // Raspberry Pi'den gelen veriyi oku
    lastValue = Serial.parseInt(); 
    analogWrite(9, lastValue);

    Serial.print("Gelen deger: ");
    Serial.println(lastValue);
    Serial.print("PWM degeri: ");
    Serial.println(lastValue);
  }





  delay(100); 
}
/* Raspberry pi ye usb ile baglanan Arduino ; 
		
Raspberyy pi 4 icin python kodu
```python
from gpiozero import LED
import time
import serial

def get_cpu_temp():
    temp = None
    with open("/sys/class/thermal/thermal_zone0/temp") as f:
        temp = f.read()
    return float(temp) / 1000
def scale_value(value, old_min, old_max, new_min, new_max):
    old_range = old_max - old_min
    new_range = new_max - new_min
    new_value = (((value - old_min) * new_range) / old_range) + new_min
    return new_value
def map_temp_to_value(temp):
    if int(temp) in range(30,44):
        return 0
    if temp >= 60:
        return 255
    else:
        return int(scale_value(temp, 36, 60, 80, 254))

def send_to_arduino(value, ser):
    ser.write(f"{value}\n".encode())

def func_red(ser):
    temp = get_cpu_temp()
    value = map_temp_to_value(temp)
    send_to_arduino(value, ser)
    print(temp,value)
    time.sleep(10)

if __name__ == "__main__":
    
    ser = serial.Serial('/dev/ttyUSB0', 9600)  # Adjust the serial port as necessary
    try:
        while True:
            func_red(ser)
    except KeyboardInterrupt as e:
        send_to_arduino(0,ser)

```
*/
