# Fritzing sketch ardunio_hcsr04_buzzer_led (saved by Fritzing 1.0.2b)
breadboards: 1

parts:
  J1 = Piezo Speaker
  Parça1 = Arduino Uno (Rev3)
  Parça2 = SRF05 Ultrasonic Rangefinder
  LED1 = smd LED [color="Red (633nm)" package="0603 [SMD]"]
  R1 = Resistor [tolerance=±5% resistance=220 package="0402 [SMD]"]
  R2 = Resistor [tolerance=±5% resistance=220 package="0402 [SMD]"]

nets:
  GND: J1.pin1, Parça1.GND, Parça2.GND, LED1.cathode
  N1: J1.pin2, R2.Pin_0
  N2: Parça1.D8, R2.Pin_1
  N3: Parça1.D9_PWM, R1.Pin_1
  N4: Parça1.D6_PWM, Parça2.Echo
  N5: Parça1.D7, Parça2.Trig
  5V: Parça1.5V, Parça2.VCC
  N6: LED1.anode, R1.Pin_0

// code stored in the sketch: ardunio_hcsr04_buzzer_led.ino


#define echo_pin 6
#define trig_pin 7
#define buzzer_pin 8
#define led_pin 9


int maximum_range = 50;
int minimum_range = 0;


void setup() {
  // put your setup code here, to run once:
  pinMode(trig_pin,OUTPUT);
  pinMode(echo_pin,INPUT);
  pinMode(buzzer_pin,OUTPUT);
  pinMode(led_pin,OUTPUT);
  //Serial.begin(9600);
}


void loop() {
  // put your main code here, to run repeatedly:
  int olcum = mesafe(maximum_range,minimum_range);
//  Serial.println(olcum);
  melodi(olcum*10);


}
int mesafe(int max ,int min){
  long duration,distance;
  digitalWrite(trig_pin,LOW);
  delayMicroseconds(2);
  digitalWrite(trig_pin,HIGH);
  delayMicroseconds(10);
  digitalWrite(trig_pin,LOW);
  duration = pulseIn(echo_pin,HIGH);
  distance = duration / 58.2;
  delay(50);
  if (distance > max || distance <= min)
  return 0;
  return distance;
}
int melodi(int dly){


  if (dly){
    tone(buzzer_pin, 440);
    digitalWrite(led_pin,HIGH);
    delay(dly);
    digitalWrite(led_pin,LOW);
    noTone(buzzer_pin);
    delay(dly);
    }
  }
