# Fritzing sketch ardunio_led_with_pwm (saved by Fritzing 1.0.2b)
breadboards: 1

parts:
  Parça1 = Arduino Uno (Rev3)
  U1 = POT [knob_status=50% power=0.5W package=pot_alpha_rv16af-20]
  LED1 = smd LED [color="Red (633nm)" package="0805 [SMD]"]
  R1 = Resistor [tolerance=±5% power=0.25W resistance=220 package=THT]

nets:
  N1: Parça1.A0, U1.S
  N2: Parça1.D3_PWM, R1.Pin_1
  N3: Parça1.5V, U1.A
  N4: Parça1.GND, U1.E, LED1.cathode
  N5: LED1.anode, R1.Pin_0

// code stored in the sketch: ardunio_led_with_pin.ino
# define led 3
# define pot A0



void setup() {
  // put your setup code here, to run once:


}


void loop() {
  // put your main code here, to run repeatedly:
  int deger = analogRead(pot);
  deger = map(deger,0,1023,0,255);
  // deger = deger /4 ;
  analogWrite(led,deger);
}
