# Fritzing sketch dc_motor (saved by Fritzing 1.0.2b)
breadboards: 1

parts:
  IC1 = L293D [package=THT]
  Raspberry_Pi_1 = Raspberry Pi 4 [part_number=RPI-4-b]
  VCC1 = 4 x AAA Battery Mount
  M1 = DC Motor [voltage_(max)=6V voltage_(min)=3V]

nets:
  N1: IC1.Enable_1, Raspberry_Pi_1.GPIO25
  N2: IC1.In_1, Raspberry_Pi_1.GPIO24
  N3: IC1.Out_1_(_Controlled_by_Enable_1_), M1.pin_2
  N4: IC1.0V, Raspberry_Pi_1.GND, VCC1.-
  N5: IC1.Out_2_(_Controlled_by_Enable_1_), M1.pin_1
  N6: IC1.In_2, Raspberry_Pi_1.GPIO23
  N7: IC1.+Vmotor, VCC1.+
  N8: IC1.+V, Raspberry_Pi_1.5V

notes:
  5v luk adaptör

custom parts:
  Raspberry Pi 4: The RPi4, a faster version of the awesome Raspberry Pi 2 B ARM Board with 40 pin gpio. Ready for special Raspberry Pi B+ and RPi2 Hat (Hardware attached (on) top)
