# Fritzing sketch mpu6050 (saved by Fritzing 1.0.2b)

parts:
  GY1 = MPU-6050 Board GY-521 [form="♀ (female)" package=THT]
  Raspberry_Pi_1 = Raspberry Pi 4 [part_number=RPI-4-b]

nets:
  N1: GY1.pin1, Raspberry_Pi_1.3v3
  N2: GY1.pin2, Raspberry_Pi_1.GND
  N3: GY1.pin3, Raspberry_Pi_1.GPIO3
  N4: GY1.pin4, Raspberry_Pi_1.GPIO2

custom parts:
  MPU-6050 Board GY-521: Acelerometro y Giroscopio MPU-6050 Board GY-521
  Raspberry Pi 4: The RPi4, a faster version of the awesome Raspberry Pi 2 B ARM Board with 40 pin gpio. Ready for special Raspberry Pi B+ and RPi2 Hat (Hardware attached (on) top)
