# Fritzing sketch pir sensor (saved by Fritzing 1.0.2b)
breadboards: 1

parts:
  Parça1 = Arduino Uno (Rev3)
  LED1 = smd LED [color="Red (633nm)" package="0603 [SMD]"]
  R1 = Resistor [tolerance=±5% resistance=220 package="0402 [SMD]"]
  Parça2 = HC-SR501 Body Sensor Module
  J1 = Piezo Speaker
  R2 = Resistor [tolerance=±5% resistance=220 package="0402 [SMD]"]

nets:
  N1: Parça1.D8, R1.Pin_1
  N2: Parça1.D2, Parça2.OUT
  5V: Parça1.5V, Parça2.VCC
  GND: Parça1.GND, LED1.cathode, Parça2.GND, J1.pin1
  N3: LED1.anode, R1.Pin_0
  N4: J1.pin2, R2.Pin_1

custom parts:
  HC-SR501 Body Sensor Module: Pyroelectric Infrared PIR Motion Sensor Detector Module

// code stored in the sketch: pir_sensor.ino
// PIR sensörünün ba?l? oldu?u pin
int pirPin = 2;
// LED'in ba?l? oldu?u pin (iste?e ba?l?)
int ledPin = 8;
// PIR sensöründen gelen okuma de?eri
int pirValue = 0;


void setup() {
  // PIR sensör pinini giri? olarak ayarla
  pinMode(pirPin, INPUT);
  // LED pinini ç?k?? olarak ayarla (iste?e ba?l?)
  pinMode(ledPin, OUTPUT);
  // Seri ileti?imi ba?lat
  Serial.begin(9600);
}


void loop() {
  // PIR sensöründen gelen de?eri oku
  pirValue = digitalRead(pirPin);
  // Seri monitörde de?eri yazd?r
  Serial.println(pirValue);


  // Hareket alg?land???nda (pirValue == HIGH)
  if (pirValue == HIGH) {
    // LED'i yak (iste?e ba?l?)
    digitalWrite(ledPin, HIGH);
    // ?lgili i?lemi yap
    //Serial.println("Hareket alg?land?!");
  } else {
    // LED'i söndür (iste?e ba?l?)
    digitalWrite(ledPin, LOW);
  }


  // K?sa bir süre bekle
  delay(1000);
}
