# Fritzing sketch transistor (saved by Fritzing 1.0.2b)
breadboards: 1

parts:
  Q1 = PNP-Transistor [package="TO92 [THT]"]
  Q2 = NPN-Transistor [package="TO92 [THT]"]
  Parça1 = Arduino Uno (Rev3)
  R1 = Resistor [tolerance=±5% power=0.25W resistance=1000 package=THT]
  LED1 = smd LED [color="Red (633nm)" package="0603 [SMD]"]
  R2 = Resistor [tolerance=±5% power=0.25W resistance=220 package=THT]
  LED2 = smd LED [color="Red (633nm)" package="0603 [SMD]"]
  R3 = Resistor [tolerance=±5% power=0.25W resistance=220 package=THT]

nets:
  N1: Q1.E, LED1.anode
  N2: Q1.B, Q2.B, R1.Pin_1
  N3: Q1.C, Parça1.5V, LED2.anode
  N4: Q2.E, R3.Pin_0
  N5: Q2.C, Parça1.GND, R2.Pin_1
  N6: Parça1.D13/SCK, R1.Pin_0
  N7: LED1.cathode, R2.Pin_0
  N8: LED2.cathode, R3.Pin_1
