# Fritzing sketch transistor_2 (saved by Fritzing 1.0.2b)
breadboards: 1

parts:
  Q1 = PNP-Transistor [package="TO92 [THT]"]
  Q2 = NPN-Transistor [package="TO92 [THT]"]
  Parça1 = Arduino Uno (Rev3)
  LED1 = smd LED [color="Red (633nm)" package="0603 [SMD]"]
  R2 = Resistor [tolerance=±5% power=0.25W resistance=220 package=THT]
  LED2 = smd LED [color="Red (633nm)" package="0603 [SMD]"]
  R3 = Resistor [tolerance=±5% power=0.25W resistance=220 package=THT]
  R4 = Resistor [tolerance=±5% power=0.25W resistance=1000 package=THT]  # not connected

nets:
  N1: Q1.E, R3.Pin_0
  N2: Q1.C, Parça1.5V, LED1.anode
  N3: Q2.E, R2.Pin_0
  N4: Q2.C, Parça1.GND, LED2.cathode
  N5: LED1.cathode, R2.Pin_1
  N6: LED2.anode, R3.Pin_1
