# Fritzing sketch uno_butonlu_led (saved by Fritzing 1.0.2b)
breadboards: 1

parts:
  Parça1 = Arduino Uno (Rev3)
  S1 = Momentary Switch [package=ksa_sealed_tac_switch]
  R1 = Resistor [tolerance=±5% power=0.25W resistance=1k package=THT]
  R2 = Resistor [tolerance=±5% power=0.25W resistance=220 package=THT]
  LED1 = LED - 5mm [color="Red (633nm)" current=0.030A package="5 mm [THT]"]

nets:
  N1: Parça1.D8, S1.1, R1.Pin_0
  N2: Parça1.D10_PWM/SS, R2.Pin_1
  N3: Parça1.5V, S1.3
  N4: Parça1.GND, R1.Pin_1, LED1.cathode
  N5: R2.Pin_0, LED1.anode
