# Fritzing sketch uno_relay_with_fan_5v (saved by Fritzing 1.0.2b)

parts:
  Parça1 = Arduino Uno (Rev3)
  KY-1 = Keyes Relay [package=THT]
  JACK1 = 2.1mm Barrel Jack with Terminal Block
  F1 = Fan - Ventilador [package=THT]

nets:
  N1: Parça1.D7, KY-1.signal
  N2: Parça1.5V, KY-1.power
  GND: Parça1.GND, KY-1.ground, JACK1.NEG, F1.GND
  N3: KY-1.C, JACK1.POS
  N4: KY-1.NO, F1.5V

custom parts:
  Keyes Relay: The Keyes 5V relay module is suitable for SCM development, home appliance control. It uses a 5V~12V TIL control signal which can control DC / AC signal.
  Fan - Ventilador: Ventilador de 2 pines, se encuentra comunmente en computadoras de escritorio
